# Fritzing sketch confort_blinker_new (saved by Fritzing 0.7.0b)
perfboards: 1
breadboards: 6

parts:
  C1 = Ceramic Capacitor [capacitance=22pF package="100 mil [THT, multilayer]"]
  C2 = Ceramic Capacitor [capacitance=22pF package="100 mil [THT, multilayer]"]
  C3 = Electrolytic Capacitor [capacitance=0.1mF voltage=16V package="100 mil [THT, electrolytic]"]
  C4 = Electrolytic Capacitor [capacitance=0.1mF voltage=20V package="100 mil [THT, electrolytic]"]
  XTAL1 = Crystal [frequency="16 Mhz" package=THT]
  C5 = Ceramic Capacitor [capacitance=100nF voltage=16V package="100 mil [THT, multilayer]"]
  C6 = Ceramic Capacitor [capacitance=100nF package="100 mil [THT, multilayer]"]
  U2 = atmega168 [package="DIP28 [THT]"]
  R1 = Resistor [tolerance=±5% resistance=10k package=THT]
  J2 = Screw terminal - 2 pins [part_number=napajanie package=THT]
  R2 = Resistor [tolerance=±5% resistance=1M package=THT]
  Q1 = NPN-Transistor [part_number=BC547 package="TO92 [THT]"]
  Q2 = NPN-Transistor [part_number=BC547 package="TO92 [THT]"]
  D3 = Rectifier Diode [part_number=1N4007 package="300 mil [THT]"]
  K2 = Relay [part_number=FRS1B-S package=THT]
  R3 = Resistor [tolerance=±5% resistance=10k package=THT]
  R4 = Resistor [tolerance=±5% resistance=10k package=THT]
  R5 = Resistor [tolerance=±5% resistance=10k package=THT]
  R6 = Resistor [tolerance=±5% resistance=10k package=THT]
  J3 = Screw terminal - 2 pins [part_number="indikatory na palubke" package=THT]
  R8 = Resistor [tolerance=±5% resistance=1.2k package=THT]
  R9 = Resistor [tolerance=±5% resistance=1.2k package=THT]
  D5 = Zener Diode [part_number=1N4732A breakdown_voltage=5.1V package="300 mil [THT]"]
  D6 = Zener Diode [part_number=1N4732A breakdown_voltage=5.1V package="300 mil [THT]"]
  R10 = Resistor [tolerance=±5% resistance=10k package=THT]
  R11 = Resistor [tolerance=±5% resistance=10k package=THT]
  U3 = Voltage Regulator - 5V [package="TO220 [THT]"]
  D12 = Rectifier Diode [part_number=1N4001 package="300 mil [THT]"]
  J6 = Screw terminal - 2 pins [part_number=spinace package=THT]
  J7 = Screw terminal - 2 pins [part_number=toBSI package=THT]
  D13 = Rectifier Diode [part_number=1N4001 package="300 mil [THT]"]
  D15 = Rectifier Diode [part_number=1N4007 package="300 mil [THT]"]
  D16 = Rectifier Diode [part_number=1N4007 package="300 mil [THT]"]
  K1 = Relay [part_number=FRS1B-S package=THT]
  D4 = Rectifier Diode [part_number=1N4007 package="300 mil [THT]"]

nets:
  N1: C1.0, C2.0, C3.-, C4.-, C5.0, C6.0, U2.Pin_8, U2.Pin_22, J2.pin1, Q1.E, Q2.E, K2.C1, K2.C2, D5.anode, D6.anode, R10.Pin_0, R11.Pin_0, U3.GND, K1.C1, K1.C2
  N2: C1.1, XTAL1.pin_0, U2.Pin_10, R2.Pin_1
  N3: C2.1, XTAL1.pin_1, U2.Pin_9, R2.Pin_0
  N4: C3.+, C6.1, U2.Pin_7, U2.Pin_20, R1.Pin_0, D3.cathode, K2.COIL2, R5.Pin_0, R6.Pin_1, U3.output_voltage, K1.COIL2, D4.cathode
  N5: C4.+, C5.1, J2.pin2, U3.input_voltage
  N6: U2.Pin_1, R1.Pin_1
  N7: U2.Pin_2, R8.Pin_1, D5.cathode, R10.Pin_1
  N8: U2.Pin_3, R9.Pin_1, D6.cathode, R11.Pin_1
  N9: U2.Pin_6, R6.Pin_0, D13.cathode
  N10: U2.Pin_11, R5.Pin_1, D12.cathode
  N11: U2.Pin_12, R3.Pin_0
  N12: U2.Pin_13, R4.Pin_0
  N13: Q1.B, R3.Pin_1
  N14: Q1.C, K2.COIL1, D4.anode
  N15: Q2.B, R4.Pin_1
  N16: Q2.C, D3.anode, K1.COIL1
  N17: K2.B, J7.pin1, D16.cathode
  N18: J3.pin1, R9.Pin_0
  N19: J3.pin2, R8.Pin_0
  N20: D12.anode, J6.pin1, J6.pin2, D13.anode, D15.anode, D16.anode
  N21: J7.pin2, D15.cathode, K1.B

notes:
  konnektor prepinaca blinkrov (9NR)
  povodny sedy cislo 233 (GR) do svorky 4A
  povony hnedy cislo 234 (MR) do svorky 2A
  konektor na BSI 26JN
  povodny sedy cislo 233 (GR) do svorky 23
  povodny hnedy cislo 234 (MR) do svorky 10
  konektor BSI 16VE
  svorky 10 a 4 (indikatory)
  kable:
  zeleny 2334 (GR)
  biely 2334 (BE)
  Blinker tripling
